# Fritzing sketch LidarLayout (saved by Fritzing 0.9.6b)
breadboards: 1

parts:
  U1 = ESP32S-HiLetgo [part_number=ESP32S-HiLetgo]
  IC5 = DIP - 6 pins [chip_label=IC package="DIP (Dual Inline) [THT]"]
  IC1 = 28BYJ-48 Stepper Driver [package="DIP (Dual Inline) [THT]"]
  IC2 = 28BYJ-48 Stepper Driver [package="DIP (Dual Inline) [THT]"]
  IC4 = DIP - 6 pins [chip_label=IC package="DIP (Dual Inline) [THT]"]
  IC3 = DIP - 6 pins [chip_label=IC package="DIP (Dual Inline) [THT]"]

nets:
  N1: U1.GPIO33, IC2.IN4
  N2: U1.GPIO25, IC2.IN3
  N3: U1.GPIO26, IC2.IN2
  N4: U1.GPIO27, IC2.IN1
  GND: U1.GND, IC5.GND, IC5.Config, IC1.GND, IC2.GND
  N5: U1.GPIO13, IC5.Multiplexing_out
  VCC: U1.VIN, IC5.5V, IC1.VCC, IC2.VCC
  N6: U1.GPIO16, IC1.IN1
  N7: U1.GPIO17, IC1.IN2
  N8: U1.GPIO18, IC1.IN3
  N9: U1.GPIO19, IC1.IN4
  N10: U1.GPIO21, IC5.SDA/RXD
  N11: U1.GPIO22, IC5.SCL/TXD
  N12: IC1.5V_Stepper, IC4.5V
  N13: IC1.Coil_1, IC4.C1
  N14: IC1.Coil_3, IC4.C3
  N15: IC1.Coil_2, IC4.C2
  N16: IC1.Coil_4, IC4.C4
  N17: IC2.5V_Stepper, IC3.5V
  N18: IC2.Coil_1, IC3.C1
  N19: IC2.Coil_3, IC3.C3
  N20: IC2.Coil_2, IC3.C2
  N21: IC2.Coil_4, IC3.C4

custom parts:
  ESP32S-HiLetgo: HiLetgo ESP-WROOM-32 ESP32 ESP-32S Development Board 2.4GHz Dual-Mode WiFi + Bluetooth Dual Cores Microcontroller The ESP32 integrated with Antenna switches, RF Balun, power amplifiers, low-noise amplifiers, filters, and management modules, and the entire solution occupies the least area of PCB. 2.4 GHz Wi-Fi plus Bluetooth dual-mode chip, with TSMC Ultra-low power consumption 40nm technology,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
  DIP - 6 pins: A DIP stand-in part for whatever IC you want. With 6 pins on a 300mil dual inline package (DIP) footprint.
  28BYJ-48 Stepper Driver: A DIP stand-in part for whatever IC you want. With 16 pins on a 300mil dual inline package (DIP) footprint.
  DIP - 6 pins: A DIP stand-in part for whatever IC you want. With 6 pins on a 300mil dual inline package (DIP) footprint.
